# Fritzing sketch diagram (saved by Fritzing 1.0.5)
perfboards: 5

parts:
  U1 = LCD-16X2 [package=lcd-16x2_noholes]
  Компонент1 = Arduino Uno (Rev3) - ICSP
  J1 = Basic Servo
  U2 = HT8950 [package=dil18]
  FLO-30_Circuit1 = FLO-30 Circuit
  R1 = Resistor [tolerance=±5% power=0.25W resistance=220 package=THT]  # not connected
  R2 = Resistor [tolerance=±5% power=0.25W resistance=220 package=THT]  # not connected
  R3 = PHOTOCELL [package=photocell-kit]  # not connected
  R5 = 12mm Trimmer Potentiometer (Large) [maximum_resistance=10kΩ knob_status=50% power=0.5W package=THT]
  U4 = HT8950 [package=dil18]
  U5 = HT8950 [package=dil18]
  LED1 = smd LED [color="Red (633nm)" package="0805 [SMD]"]  # not connected
  LED4 = smd LED [color="Red (633nm)" package="0805 [SMD]"]  # not connected
  U6 = HT8950 [package=dil18]
  U7 = HT8950 [package=dil18]
  LED5 = smd LED [color="Red (633nm)" package="0805 [SMD]"]  # not connected
  LED6 = smd LED [color="Red (633nm)" package="0805 [SMD]"]  # not connected

nets:
  N1: U1.VO, U5.SW1
  N2: U1.RS, U5.SW0
  N3: U1.E, Компонент1.D5_PWM
  N4: U1.DB0, Компонент1.D6_PWM
  N5: U1.DB1, Компонент1.D7
  N6: U1.DB6, Компонент1.D8
  N7: U1.DB7, Компонент1.D9_PWM
  N8: U1.A, Компонент1.D10_PWM/SS
  N9: U1.K, Компонент1.D11_PWM/MOSI
  N10: Компонент1.D12/MISO, J1.vcc
  N11: Компонент1.D13/SCK, U2.TGD
  N12: Компонент1.D2, U7.AO
  N13: Компонент1.D3_PWM, U6.AO
  N14: Компонент1.D4, FLO-30_Circuit1.TX
  N15: Компонент1.5V, U4.SW0
  N16: Компонент1.GND, U5.AO
  N17: U2.VREF, U5.VDD
  GND: FLO-30_Circuit1.GND, U5.VSS
  N18: FLO-30_Circuit1.RX, U4.VDD
  N19: R5.leg1, U5.SW2
  N20: R5.leg2, U4.AUDIO
  N21: U5.AIN, U6.VSS
  N22: U5.LAMP, U7.VSS
